# Fritzing sketch BioLumen (saved by Fritzing 0.9.3b)
breadboards: 1

parts:
  Raspberry_Pi1 = Raspberry Pi B+
  DS1 = DS18B20 1-Wire Temperature Sensor [part_number=DS18B20]
  S1 = PH meter [package=THT]
  R1 = Resistor [tolerance=±5% resistance=220 package="2512 [SMD]"]
  ADC1 = MCP3008 [package=dil16]
  IC1 = L293D [package=THT]
  M1 = DC Motor
  M2 = DC Motor

nets:
  VDD: Raspberry_Pi1.3v3, DS1.VDD, ADC1.VREF, ADC1.VDD
  N1: Raspberry_Pi1.GPIO4, DS1.DQ, R1.Pin_1
  GND: Raspberry_Pi1.GND, DS1.GND, S1.pin3, R1.Pin_0, ADC1.DGND, ADC1.CS/SHDN, ADC1.AGND
  N2: Raspberry_Pi1.GPIO13, IC1.Enable_2
  N3: Raspberry_Pi1.GPIO19, IC1.In_3
  N4: Raspberry_Pi1.GPIO26, IC1.In_4
  N5: Raspberry_Pi1.GPIO21, IC1.Enable_1
  N6: Raspberry_Pi1.GPIO20, IC1.In_2
  N7: Raspberry_Pi1.GPIO16, IC1.In_1
  N8: Raspberry_Pi1.GPIO24, ADC1.Din
  N9: Raspberry_Pi1.GPIO23, ADC1.Dout
  N10: Raspberry_Pi1.GPIO18, ADC1.CLK
  N11: Raspberry_Pi1.5V, S1.pin1, IC1.+V
  N12: S1.pin2, ADC1.CH0
  N13: IC1.Out_1_(_Controlled_by_Enable_1_), M1.pin_1
  N14: IC1.Out_2_(_Controlled_by_Enable_1_), M1.pin_2
  N15: IC1.Out_3_(_Controlled_by_Enable_2_), M2.pin_1
  N16: IC1.Out_4_(_Controlled_by_Enable_2_), M2.pin_2

notes:
  3.3v
  5v
  This is what is in the .fzz file
  It can be viewed/edited with the software found at:
  http://fritzing.org/home/
  To 12v
